# Fritzing sketch circuit (saved by Fritzing 0.9.3b)

parts:
  WeMos_D1_Mini1 = WeMos D1 Mini
  HC-SR04_Sensor_1 = HC-SR04 Ultrasonic Distance Sensor
  M1 = DC Motor  # not connected
  Power_plug1 = Power plug  # not connected
  Part2 = MD10C R2
  X1 = USB Connectors [package=usb-a-h]  # not connected

nets:
  5V: WeMos_D1_Mini1.5V, HC-SR04_Sensor_1.VCC
  N1: WeMos_D1_Mini1.D3, Part2.no_name_yet#connector_1
  N2: WeMos_D1_Mini1.D4, Part2.no_name_yet#connector_2
  N3: WeMos_D1_Mini1.D6, HC-SR04_Sensor_1.TRIG
  N4: WeMos_D1_Mini1.D7, HC-SR04_Sensor_1.ECHO
  N5: WeMos_D1_Mini1.G, HC-SR04_Sensor_1.GND, Part2.no_name_yet#connector_3

notes:
  Motor Driver
  Is used by the Microcontroller Board in order to digitally control the DC Motor/tables height.
  DC Motor
  Input: DC 12V
  Speed: 72 RPM
  Can raise and lower the table.
  Power Adapter
  Input: AC 110-240V
  Output: DC 12V 5A
  USB Power Source
  Output: 3.3-5V
  This is just a USB-A to USB-Micro-B cable which powers the Microcontroller Board.
  Ultrasonic Sensor
  Used for measureing the height/distance of the table.
  Microcontroller Board
  Hosts a Web Server and has the business logic for controlling the table.
